# Fritzing sketch Photo Resistor (saved by Fritzing 0.9.3b)
breadboards: 1

parts:
  Part1 = Arduino Mega 2560 (Rev3)
  R1 = PHOTOCELL [package=photocell]
  R2 = Resistor [tolerance=±5% resistance=10k package="2512 [SMD]"]
  LED1 = smd LED [color="Red (633nm)" package="0805 [SMD]"]
  R3 = Resistor [tolerance=±5% resistance=330 package="2512 [SMD]"]

nets:
  N1: Part1.A0, R1.P$1, R2.Pin_1
  N2: Part1.5V, R1.P$2
  N3: Part1.GND, R2.Pin_0, R3.Pin_0
  N4: Part1.D22, LED1.anode
  N5: LED1.cathode, R3.Pin_1
